# Fritzing sketch wiring (saved by Fritzing 0.9.3b)
breadboards: 1

parts:
  Composant1 = Arduino Uno (Rev3)
  U1 = MIDI_CONN_FEMALE_SUPPORT [package=din_5_female_support]
  LD1 = LD
  R3 = Photocell (LDR) [package=THT]
  R4 = Resistor [tolerance=±1% resistance=10k package=THT]
  R1 = Resistor [tolerance=±1% resistance=220 package=THT]
  R2 = Resistor [tolerance=±1% resistance=220 package=THT]

nets:
  N1: Composant1.A0, R3.pin_1, R4.Pin_0
  N2: Composant1.GND, U1.NC1, LD1.cathode, R4.Pin_1
  N3: Composant1.D6_PWM, R1.Pin_0
  N4: Composant1.5V, LD1.anode, R3.pin_0, R2.Pin_0
  N5: U1.MIDI_IN, R1.Pin_1
  N6: U1.MIDI_OUT, R2.Pin_1

custom parts:
  LD: A Generic Red Dot Laser Diode Module (~5mW)
